# Fritzing sketch ServoModule (saved by Fritzing 1.0.2b)
circuit board: 5.2354cm x 9.68321cm
breadboards: 1

parts:
  C1 = Electrolytic Capacitor [capacitance=1µF voltage=35V package="100 mil [THT, electrolytic]"]
  C2 = Electrolytic Capacitor [capacitance=1µF voltage=35V package="100 mil [THT, electrolytic]"]
  C3 = Electrolytic Capacitor [capacitance=1µF voltage=35V package="100 mil [THT, electrolytic]"]
  D3 = Rectifier Diode [part_number=1N4001 package="300 mil [THT]"]
  JP1 = FTDI_BASIC [package=ftdi_basic]
  JP2 = FTDI_BASIC [package=ftdi_basic]
  JP3 = FTDI_BASIC [package=ftdi_basic]
  GND = FTDI_BASIC [package=ftdi_basic]
  V = FTDI_BASIC [package=ftdi_basic]
  C4 = Electrolytic Capacitor [capacitance=1µF voltage=35V package="100 mil [THT, electrolytic]"]
  C5 = Electrolytic Capacitor [capacitance=1µF voltage=35V package="100 mil [THT, electrolytic]"]
  C6 = Electrolytic Capacitor [capacitance=1µF voltage=35V package="100 mil [THT, electrolytic]"]
  SIGNAL_IN = FTDI_BASIC [package=ftdi_basic]
  Fuse1 = Fuse with Handler [part_number=Htc-15m]
  D2 = Rectifier Diode [part_number=1N4001 package="300 mil [THT]"]
  C7 = Capacitor [package=cap-pth-small2]
  C8 = Capacitor [package=cap-pth-small2]
  C9 = Capacitor [package=cap-pth-small2]
  C10 = Capacitor [package=cap-pth-small2]
  C11 = Capacitor [package=cap-pth-small2]
  C12 = Capacitor [package=cap-pth-small2]
  VREG = Voltage Regulator - Variable [package="TO220 [THT]"]
  Jump_FUSE = Solder Jumper [package=sj_2s-notrace]
  D1 = Rectifier Diode [part_number=1N4001 package="300 mil [THT]"]
  V_Jump = Solder Jumper [package=sj_2s-trace]
  Jump_VREG = Solder Jumper [package=sj_2s-notrace]
  VIN = Camdenboss CTB0158-2 [part_number=CTB0158-2 package=THT]
  VOUT = Camdenboss CTB0158-2 [part_number=CTB0158-2 package=THT]

nets:
  N1: C1.-, C2.-, C3.-, JP1.6, JP1.3, JP2.6, JP2.3, JP3.6, JP3.3, GND.5, GND.1, GND.6, GND.2, GND.3, GND.4, C4.-, C5.-, C6.-, C7.2, C8.2, C9.2, C10.2, C11.2, C12.2, VREG.OUT, VIN.pin1, VOUT.pin1
  N2: C1.+, C2.+, C3.+, D3.cathode, JP1.5, JP1.2, JP2.5, JP2.2, JP3.5, JP3.2, C4.+, C5.+, C6.+, C7.1, C8.1, C9.1, C10.1, C11.1, C12.1
  N3: D3.anode, D2.cathode
  N4: JP1.1, SIGNAL_IN.5
  N5: JP1.4, SIGNAL_IN.6
  N6: JP2.1, SIGNAL_IN.3
  N7: JP2.4, SIGNAL_IN.4
  N8: JP3.1, SIGNAL_IN.1
  N9: JP3.4, SIGNAL_IN.2
  N10: V.5, V.1, V.6, V.2, V.3, V.4, V_Jump.1
  N11: Fuse1.Connector1, Jump_FUSE.2, VIN.pin2
  N12: Fuse1.Connector2, D2.anode, VREG.IN, Jump_FUSE.1, Jump_VREG.1
  N13: VREG.ADJ, D1.anode, Jump_VREG.2
  N14: D1.cathode, V_Jump.2, VOUT.pin2

notes:
  THS-DEVS
  Servo Module v2.1
  +
  -
